# Fritzing sketch S4_SmartDevices_PauwelsWard_ExamSchematic (saved by Fritzing 0.9.3b)
breadboards: 1

parts:
  Onderdeel1 = Arduino Uno (Rev3) - ICSP
  J1 = Basic Servo
  M1 = DC Motor
  M2 = DC Motor
  IC1 = H-Bridge [package=THT]
  LED1 = LED - 5mm [color="Red (633nm)" package="5 mm [THT]"]
  LED2 = LED - 5mm [color="Red (633nm)" package="5 mm [THT]"]
  LED3 = LED - 5mm [color="Red (633nm)" package="5 mm [THT]"]
  LED4 = LED - 5mm [color="Red (633nm)" package="5 mm [THT]"]
  LED5 = LED - 5mm [color="Red (633nm)" package="5 mm [THT]"]
  IR1 = TSOP312.., 314.. [package=THT]
  Onderdeel2 = Bluetooth HC-05 Macho
  R1 = Resistor [tolerance=±5% resistance=220 package="2010 [SMD]"]
  R2 = Resistor [tolerance=±5% resistance=220 package="2010 [SMD]"]
  R3 = Resistor [tolerance=±5% resistance=220 package="2010 [SMD]"]
  R4 = Resistor [tolerance=±5% resistance=220 package="2010 [SMD]"]
  R5 = Resistor [tolerance=±5% resistance=220 package="2010 [SMD]"]
  R6 = Resistor [tolerance=±5% resistance=220 package="2010 [SMD]"]
  BAT1 = BC9VPC [package=bc9vpc]
  S1 = Pushbutton [package="[SMD]"]
  R7 = Resistor [tolerance=±5% resistance=220 package="2010 [SMD]"]
  R8 = Resistor [tolerance=±5% resistance=220 package="2010 [SMD]"]
  Infrared_Light = smd LED [color="Red (633nm)" package="1206 [SMD]"]

nets:
  N1: Onderdeel1.A0, LED1.anode
  N2: Onderdeel1.A1, LED2.anode
  N3: Onderdeel1.A2, LED3.anode
  N4: Onderdeel1.A3, LED4.anode
  N5: Onderdeel1.A4/SDA, LED5.anode
  N6: Onderdeel1.A5/SCL, Infrared_Light.anode
  N7: Onderdeel1.D8, IC1.1_2EN
  N8: Onderdeel1.D11_PWM/MOSI, IC1.3_4EN
  N9: Onderdeel1.D12/MISO, IC1.3A
  N10: Onderdeel1.D13/SCK, IC1.4A
  GND: Onderdeel1.GND, J1.gnd, IC1.GND1, IC1.GND2, IR1.Vs, Onderdeel2.GND, R1.Pin_0, R2.Pin_0, R3.Pin_0, R4.Pin_0, R5.Pin_0, R7.Pin_0, R8.Pin_0
  N11: Onderdeel1.D0/RX, R6.Pin_0
  N12: Onderdeel1.D1/TX, Onderdeel2.TXD
  N13: Onderdeel1.D2, S1.Pin_1, S1.Pin_2, R7.Pin_1
  N14: Onderdeel1.D4, IR1.GND
  N15: Onderdeel1.D5_PWM, J1.pulse
  N16: Onderdeel1.D6_PWM, IC1.2A
  N17: Onderdeel1.D7, IC1.1A
  3V3: Onderdeel1.3V3, Onderdeel2.VCC
  5V: Onderdeel1.5V, J1.vcc, IC1.VCC1, IR1.Data, S1.Pin_3, S1.Pin_4
  N18: M1.pin_1, IC1.4Y
  N19: M1.pin_2, IC1.3Y
  N20: M2.pin_1, IC1.1Y
  N21: M2.pin_2, IC1.2Y
  N22: IC1.VCC2, BAT1.V+
  GND3: IC1.GND3, IC1.GND4, BAT1.V-
  N23: LED1.cathode, R4.Pin_1
  N24: LED2.cathode, R1.Pin_1
  N25: LED3.cathode, R5.Pin_1
  N26: LED4.cathode, R3.Pin_1
  N27: LED5.cathode, R2.Pin_1
  N28: Onderdeel2.RXD, R6.Pin_1
  N29: R8.Pin_1, Infrared_Light.cathode
